# Fritzing sketch i2c-GY-NEO6MV2 (saved by Fritzing 0.9.3b)

parts:
  M1 = NEO-6M GPS Module [part_number=GY-GPS6MV2]
  MCU1 = Raspberry Pi Zero
  パーツ1 = Arduino Pro Mini (3.3V)

nets:
  GND: M1.GND, MCU1.pin_6, MCU1.pin_14, MCU1.pin_34, パーツ1.GND
  N1: M1.Tx, パーツ1.D10
  VCC: M1.Vcc, MCU1.pin_1, MCU1.pin_17, パーツ1.VCC
  N2: MCU1.pin_3, パーツ1.A4
  N3: MCU1.pin_5, パーツ1.A5

notes:
  Arduino Pro Mini 3.3V (8MHz)
  SCL
  SDA
  3V3

custom parts:
  NEO-6M GPS Module: GY-GPS6MV2 NEO-6M GPS Module Module based on U-blox NEO-6M GPS engine, incorporating regulator for 3.3-5V DC input, MS621FE-compatible rechargeable battery for backup and EEPROM for storing configuration settings. Links: NEO-6 series product information page NEO-6 Datasheet
  Raspberry Pi Zero: The Raspberry Pi Zero is half the size of a Model A+, with twice the utility. A tiny Raspberry Pi that’s affordable enough for any project! · 1Ghz, Single-core CPU · 512MB RAM · Mini HDMI and USB On-The-Go ports · Micro USB power · HAT-compatible 40-pin header. Jan 2018: In this version schematic has been changed so the pins match the GPIO connector. I.e. the left hand pins are all the pins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
